// Logisim project AES.circ as structural Verilog: 14 circuits, main circuit main
module main (
);

  raw_shift raw_shift_1 ();  // open: in0, in4, in8, in12, in1, in5, in9, in13, in2, in6, in10, in14, in3, in7, in11, in15, out0, out4, out8, out12, out13, out1, out5, out9, out10, out14, out2, out6, out7, out11, out15, out3
endmodule

module one_turn (
  input  [7:0] in0,
  input  [7:0] in1,
  input  [7:0] in2,
  input  [7:0] in3,
  input  [7:0] in4,
  input  [7:0] in5,
  input  [7:0] in6,
  input  [7:0] in7,
  input  [7:0] in8,
  input  [7:0] in9,
  input  [7:0] in10,
  input  [7:0] in11,
  input  [7:0] in12,
  input  [7:0] in13,
  input  [7:0] in14,
  input  [7:0] in15,
  input  [7:0] kin0,
  input  [7:0] kin1,
  input  [7:0] kin2,
  input  [7:0] kin3,
  input  [7:0] kin4,
  input  [7:0] kin4_2,
  input  [7:0] kin6,
  input  [7:0] kin7,
  input  [7:0] kin8,
  input  [7:0] kin9,
  input  [7:0] kin10,
  input  [7:0] kin11,
  input  [7:0] kin12,
  input  [7:0] kin13,
  input  [7:0] kin14,
  input  [7:0] kin15,
  input  [3:0] turn_number,
  output [7:0] out0,
  output [7:0] out1,
  output [7:0] out2,
  output [7:0] out3,
  output [7:0] out4,
  output [7:0] out5,
  output [7:0] out6,
  output [7:0] out7,
  output [7:0] out8,
  output [7:0] out9,
  output [7:0] out10,
  output [7:0] out11,
  output [7:0] out12,
  output [7:0] out13,
  output [7:0] out14,
  output [7:0] out15,
  output [7:0] kout0,
  output [7:0] kout1,
  output [7:0] kout2,
  output [7:0] kout3,
  output [7:0] kout4,
  output [7:0] kout4_2,
  output [7:0] kout6,
  output [7:0] kout7,
  output [7:0] kout8,
  output [7:0] kout9,
  output [7:0] kout10,
  output [7:0] kout11,
  output [7:0] kout12,
  output [7:0] kout13,
  output [7:0] kout14,
  output [7:0] kout15
);

  wire [7:0] byte_substitute_1_out0, byte_substitute_1_out1, byte_substitute_1_out2, byte_substitute_1_out3,
       byte_substitute_1_out4, byte_substitute_1_out5, byte_substitute_1_out6, byte_substitute_1_out7,
       byte_substitute_1_out8, byte_substitute_1_out9, byte_substitute_1_out10, byte_substitute_1_out11,
       byte_substitute_1_out12, byte_substitute_1_out13, byte_substitute_1_out14, byte_substitute_1_out15,
       raw_shift_1_out0, raw_shift_1_out1, raw_shift_1_out2, raw_shift_1_out3, raw_shift_1_out4,
       raw_shift_1_out5, raw_shift_1_out6, raw_shift_1_out7, raw_shift_1_out8, raw_shift_1_out9,
       raw_shift_1_out10, raw_shift_1_out11, raw_shift_1_out12, raw_shift_1_out13, raw_shift_1_out14,
       raw_shift_1_out15, subkey_add_1_out0, subkey_add_1_out1, subkey_add_1_out2, subkey_add_1_out3,
       subkey_add_1_out4, subkey_add_1_out5, subkey_add_1_out6, subkey_add_1_out7, subkey_add_1_out8,
       subkey_add_1_out9, subkey_add_1_out10, subkey_add_1_out11, subkey_add_1_out12, subkey_add_1_out13,
       subkey_add_1_out14, subkey_add_1_out15;

  byte_substitute byte_substitute_1 (
    .in0(subkey_add_1_out0), .in1(subkey_add_1_out8), .in2(subkey_add_1_out1), .in3(subkey_add_1_out9),
    .in4(subkey_add_1_out2), .in5(subkey_add_1_out10), .in6(subkey_add_1_out3), .in7(subkey_add_1_out11),
    .in8(subkey_add_1_out4), .in9(subkey_add_1_out12), .in10(subkey_add_1_out5), .in11(subkey_add_1_out13),
    .in12(subkey_add_1_out6), .in13(subkey_add_1_out14), .in14(subkey_add_1_out7), .in15(subkey_add_1_out15),
    .out0(byte_substitute_1_out0), .out1(byte_substitute_1_out1), .out2(byte_substitute_1_out2),
    .out3(byte_substitute_1_out3), .out4(byte_substitute_1_out4), .out5(byte_substitute_1_out5),
    .out6(byte_substitute_1_out6), .out7(byte_substitute_1_out7), .out8(byte_substitute_1_out8),
    .out9(byte_substitute_1_out9), .out10(byte_substitute_1_out10), .out11(byte_substitute_1_out11),
    .out12(byte_substitute_1_out12), .out13(byte_substitute_1_out13), .out14(byte_substitute_1_out14),
    .out15(byte_substitute_1_out15));
  subkey_add subkey_add_1 (
    .in0(in0), .in8(in8), .kin0(kin0), .kin8(kin8), .in1(in1), .in9(in9), .kin1(kin1), .kin9(kin9),
    .in2(in2), .in10(in10), .kin2(kin2), .kin10(kin10), .in3(in3), .in11(in11), .kin3(kin3), .kin11(kin11),
    .in4(in4), .in12(in12), .kin4(kin4), .kin12(kin12), .in5(in5), .in13(in13), .kin5(kin4_2), .kin13(kin13),
    .in6(in6), .in14(in14), .kin6(kin6), .kin14(kin14), .in7(in7), .in15(in15), .kin7(kin7), .kin15(kin15),
    .out0(subkey_add_1_out0), .out8(subkey_add_1_out8), .out1(subkey_add_1_out1), .out9(subkey_add_1_out9),
    .out2(subkey_add_1_out2), .out10(subkey_add_1_out10), .out3(subkey_add_1_out3),
    .out11(subkey_add_1_out11), .out4(subkey_add_1_out4), .out12(subkey_add_1_out12),
    .out5(subkey_add_1_out5), .out13(subkey_add_1_out13), .out6(subkey_add_1_out6),
    .out14(subkey_add_1_out14), .out7(subkey_add_1_out7), .out15(subkey_add_1_out15));
  key_gen_oneturn key_gen_oneturn_1 (
    .kin0(kin0), .kin1(kin1), .kin2(kin2), .kin3(kin3), .kin4(kin4), .kin4_2(kin4_2), .kin6(kin6),
    .kin7(kin7), .kin8(kin8), .kin9(kin9), .kin10(kin10), .kin11(kin11), .kin12(kin12), .kin13(kin13),
    .kin14(kin14), .kin15(kin15), .turn_number(turn_number), .kout0(kout0), .kout1(kout1), .kout2(kout2),
    .kout3(kout3), .kout4(kout4), .kout4_2(kout4_2), .kout6(kout6), .kout7(kout7), .kout8(kout8),
    .kout9(kout9), .kout10(kout10), .kout11(kout11), .kout12(kout12), .kout13(kout13), .kout14(kout14),
    .kout15(kout15));
  raw_shift raw_shift_1 (
    .in0(byte_substitute_1_out0), .in4(byte_substitute_1_out4), .in8(byte_substitute_1_out8),
    .in12(byte_substitute_1_out12), .in1(byte_substitute_1_out1), .in5(byte_substitute_1_out5),
    .in9(byte_substitute_1_out9), .in13(byte_substitute_1_out13), .in2(byte_substitute_1_out2),
    .in6(byte_substitute_1_out6), .in10(byte_substitute_1_out10), .in14(byte_substitute_1_out14),
    .in3(byte_substitute_1_out3), .in7(byte_substitute_1_out7), .in11(byte_substitute_1_out11),
    .in15(byte_substitute_1_out15), .out0(raw_shift_1_out0), .out4(raw_shift_1_out4),
    .out8(raw_shift_1_out8), .out12(raw_shift_1_out12), .out13(raw_shift_1_out13), .out1(raw_shift_1_out1),
    .out5(raw_shift_1_out5), .out9(raw_shift_1_out9), .out10(raw_shift_1_out10), .out14(raw_shift_1_out14),
    .out2(raw_shift_1_out2), .out6(raw_shift_1_out6), .out7(raw_shift_1_out7), .out11(raw_shift_1_out11),
    .out15(raw_shift_1_out15), .out3(raw_shift_1_out3));
  column_mix column_mix_1 (
    .in0(raw_shift_1_out0), .in1(raw_shift_1_out1), .in2(raw_shift_1_out2), .in3(raw_shift_1_out3),
    .in4(raw_shift_1_out4), .in5(raw_shift_1_out5), .in6(raw_shift_1_out6), .in7(raw_shift_1_out7),
    .in8(raw_shift_1_out8), .in9(raw_shift_1_out9), .in10(raw_shift_1_out10), .in11(raw_shift_1_out11),
    .in12(raw_shift_1_out12), .in13(raw_shift_1_out13), .in14(raw_shift_1_out14), .in15(raw_shift_1_out15),
    .out0(out0), .out1(out1), .out2(out2), .out3(out3), .out4(out4), .out5(out5), .out6(out6), .out7(out7),
    .out8(out8), .out9(out9), .out10(out10), .out11(out11), .out12(out12), .out13(out13), .out14(out14),
    .out15(out15));
endmodule

module key_gen_oneturn (
  input  [7:0] kin0,
  input  [7:0] kin1,
  input  [7:0] kin2,
  input  [7:0] kin3,
  input  [7:0] kin4,
  input  [7:0] kin4_2,
  input  [7:0] kin6,
  input  [7:0] kin7,
  input  [7:0] kin8,
  input  [7:0] kin9,
  input  [7:0] kin10,
  input  [7:0] kin11,
  input  [7:0] kin12,
  input  [7:0] kin13,
  input  [7:0] kin14,
  input  [7:0] kin15,
  input  [3:0] turn_number,
  output [7:0] kout0,
  output [7:0] kout1,
  output [7:0] kout2,
  output [7:0] kout3,
  output [7:0] kout4,
  output [7:0] kout4_2,
  output [7:0] kout6,
  output [7:0] kout7,
  output [7:0] kout8,
  output [7:0] kout9,
  output [7:0] kout10,
  output [7:0] kout11,
  output [7:0] kout12,
  output [7:0] kout13,
  output [7:0] kout14,
  output [7:0] kout15
);

  wire [31:0] key_gen_g_1_out;

  key_gen_g key_gen_g_1 (.in({kin12, kin13, kin14, kin15}), .turn_number(turn_number), .out(key_gen_g_1_out));
  assign {kout0, kout1, kout2, kout3} = key_gen_g_1_out ^ {kin0, kin1, kin2, kin3};  // XOR_Gate xor_1, 32 bits wide
  assign {kout4, kout4_2, kout6, kout7} = {kout0, kout1, kout2, kout3} ^ {kin4, kin4_2, kin6, kin7};  // XOR_Gate xor_2, 32 bits wide
  assign {kout8, kout9, kout10, kout11} = {kout4, kout4_2, kout6, kout7} ^ {kin8, kin9, kin10, kin11};  // XOR_Gate xor_3, 32 bits wide
  assign {kout12, kout13, kout14, kout15} = {kout8, kout9, kout10, kout11} ^ {kin12, kin13, kin14, kin15};  // XOR_Gate xor_4, 32 bits wide
endmodule

module subkey_add (
  input  [7:0] in0,
  input  [7:0] in8,
  input  [7:0] kin0,
  input  [7:0] kin8,
  input  [7:0] in1,
  input  [7:0] in9,
  input  [7:0] kin1,
  input  [7:0] kin9,
  input  [7:0] in2,
  input  [7:0] in10,
  input  [7:0] kin2,
  input  [7:0] kin10,
  input  [7:0] in3,
  input  [7:0] in11,
  input  [7:0] kin3,
  input  [7:0] kin11,
  input  [7:0] in4,
  input  [7:0] in12,
  input  [7:0] kin4,
  input  [7:0] kin12,
  input  [7:0] in5,
  input  [7:0] in13,
  input  [7:0] kin5,
  input  [7:0] kin13,
  input  [7:0] in6,
  input  [7:0] in14,
  input  [7:0] kin6,
  input  [7:0] kin14,
  input  [7:0] in7,
  input  [7:0] in15,
  input  [7:0] kin7,
  input  [7:0] kin15,
  output [7:0] out0,
  output [7:0] out8,
  output [7:0] out1,
  output [7:0] out9,
  output [7:0] out2,
  output [7:0] out10,
  output [7:0] out3,
  output [7:0] out11,
  output [7:0] out4,
  output [7:0] out12,
  output [7:0] out5,
  output [7:0] out13,
  output [7:0] out6,
  output [7:0] out14,
  output [7:0] out7,
  output [7:0] out15
);

  assign out0 = in0 ^ kin0;  // XOR_Gate xor_1, 8 bits wide
  assign out1 = in1 ^ kin1;  // XOR_Gate xor_2, 8 bits wide
  assign out2 = in2 ^ kin2;  // XOR_Gate xor_3, 8 bits wide
  assign out3 = in3 ^ kin3;  // XOR_Gate xor_4, 8 bits wide
  assign out4 = in4 ^ kin4;  // XOR_Gate xor_5, 8 bits wide
  assign out5 = in5 ^ kin5;  // XOR_Gate xor_6, 8 bits wide
  assign out6 = in6 ^ kin6;  // XOR_Gate xor_7, 8 bits wide
  assign out7 = in7 ^ kin7;  // XOR_Gate xor_8, 8 bits wide
  assign out8 = in8 ^ kin8;  // XOR_Gate xor_9, 8 bits wide
  assign out9 = in9 ^ kin9;  // XOR_Gate xor_10, 8 bits wide
  assign out10 = in10 ^ kin10;  // XOR_Gate xor_11, 8 bits wide
  assign out11 = in11 ^ kin11;  // XOR_Gate xor_12, 8 bits wide
  assign out12 = in12 ^ kin12;  // XOR_Gate xor_13, 8 bits wide
  assign out13 = in13 ^ kin13;  // XOR_Gate xor_14, 8 bits wide
  assign out14 = in14 ^ kin14;  // XOR_Gate xor_15, 8 bits wide
  assign out15 = in15 ^ kin15;  // XOR_Gate xor_16, 8 bits wide
endmodule

module byte_substitute (
  input  [7:0] in0,
  input  [7:0] in1,
  input  [7:0] in2,
  input  [7:0] in3,
  input  [7:0] in4,
  input  [7:0] in5,
  input  [7:0] in6,
  input  [7:0] in7,
  input  [7:0] in8,
  input  [7:0] in9,
  input  [7:0] in10,
  input  [7:0] in11,
  input  [7:0] in12,
  input  [7:0] in13,
  input  [7:0] in14,
  input  [7:0] in15,
  output [7:0] out0,
  output [7:0] out1,
  output [7:0] out2,
  output [7:0] out3,
  output [7:0] out4,
  output [7:0] out5,
  output [7:0] out6,
  output [7:0] out7,
  output [7:0] out8,
  output [7:0] out9,
  output [7:0] out10,
  output [7:0] out11,
  output [7:0] out12,
  output [7:0] out13,
  output [7:0] out14,
  output [7:0] out15
);

  s_box s_box_1 (.in(in0), .out(out0));
  s_box s_box_2 (.in(in1), .out(out1));
  s_box s_box_3 (.in(in2), .out(out2));
  s_box s_box_4 (.in(in3), .out(out3));
  s_box s_box_5 (.in(in4), .out(out4));
  s_box s_box_6 (.in(in5), .out(out5));
  s_box s_box_7 (.in(in6), .out(out6));
  s_box s_box_8 (.in(in7), .out(out7));
  s_box s_box_9 (.in(in8), .out(out8));
  s_box s_box_10 (.in(in9), .out(out9));
  s_box s_box_11 (.in(in10), .out(out10));
  s_box s_box_12 (.in(in11), .out(out11));
  s_box s_box_13 (.in(in12), .out(out12));
  s_box s_box_14 (.in(in13), .out(out13));
  s_box s_box_15 (.in(in14), .out(out14));
  s_box s_box_16 (.in(in15), .out(out15));
endmodule

module raw_shift (
  input  [7:0] in0,
  input  [7:0] in4,
  input  [7:0] in8,
  input  [7:0] in12,
  input  [7:0] in1,
  input  [7:0] in5,
  input  [7:0] in9,
  input  [7:0] in13,
  input  [7:0] in2,
  input  [7:0] in6,
  input  [7:0] in10,
  input  [7:0] in14,
  input  [7:0] in3,
  input  [7:0] in7,
  input  [7:0] in11,
  input  [7:0] in15,
  output [7:0] out0,
  output [7:0] out4,
  output [7:0] out8,
  output [7:0] out12,
  output [7:0] out13,
  output [7:0] out1,
  output [7:0] out5,
  output [7:0] out9,
  output [7:0] out10,
  output [7:0] out14,
  output [7:0] out2,
  output [7:0] out6,
  output [7:0] out7,
  output [7:0] out11,
  output [7:0] out15,
  output [7:0] out3
);


  assign out0 = in0;
  assign out1 = in5;
  assign out2 = in10;
  assign out3 = in15;
  assign out4 = in4;
  assign out5 = in9;
  assign out6 = in14;
  assign out7 = in3;
  assign out8 = in8;
  assign out9 = in13;
  assign out10 = in2;
  assign out11 = in7;
  assign out12 = in12;
  assign out13 = in1;
  assign out14 = in6;
  assign out15 = in11;
endmodule

module column_mix (
  input  [7:0] in0,
  input  [7:0] in1,
  input  [7:0] in2,
  input  [7:0] in3,
  input  [7:0] in4,
  input  [7:0] in5,
  input  [7:0] in6,
  input  [7:0] in7,
  input  [7:0] in8,
  input  [7:0] in9,
  input  [7:0] in10,
  input  [7:0] in11,
  input  [7:0] in12,
  input  [7:0] in13,
  input  [7:0] in14,
  input  [7:0] in15,
  output [7:0] out0,
  output [7:0] out1,
  output [7:0] out2,
  output [7:0] out3,
  output [7:0] out4,
  output [7:0] out5,
  output [7:0] out6,
  output [7:0] out7,
  output [7:0] out8,
  output [7:0] out9,
  output [7:0] out10,
  output [7:0] out11,
  output [7:0] out12,
  output [7:0] out13,
  output [7:0] out14,
  output [7:0] out15
);

  column_mix_col column_mix_col_1 (
    .in0(in0), .in1(in1), .in2(in2), .in3(in3), .out0(out0), .out1(out1), .out2(out2), .out3(out3));
  column_mix_col column_mix_col_2 (
    .in0(in4), .in1(in5), .in2(in6), .in3(in7), .out0(out4), .out1(out5), .out2(out6), .out3(out7));
  column_mix_col column_mix_col_3 (
    .in0(in8), .in1(in9), .in2(in10), .in3(in11), .out0(out8), .out1(out9), .out2(out10), .out3(out11));
  column_mix_col column_mix_col_4 (
    .in0(in12), .in1(in13), .in2(in14), .in3(in15), .out0(out12), .out1(out13), .out2(out14), .out3(out15));
endmodule

module register256 (
  input  [7:0] in0,
  input  [7:0] in8,
  input  [7:0] in1,
  input  [7:0] in9,
  input  [7:0] in2,
  input  [7:0] in10,
  input  [7:0] in3,
  input  [7:0] in11,
  input  [7:0] in4,
  input  [7:0] in12,
  input  [7:0] in5,
  input  [7:0] in13,
  input  [7:0] in6,
  input  [7:0] in14,
  input  [7:0] in7,
  input  [7:0] in15,
  input  [7:0] kin0,
  input  [7:0] kin8,
  input  [7:0] kin1,
  input  [7:0] kin9,
  input  [7:0] kin2,
  input  [7:0] kin10,
  input  [7:0] kin3,
  input  [7:0] kin11,
  input  [7:0] kin4,
  input  [7:0] kin12,
  input  [7:0] kin5,
  input  [7:0] kin13,
  input  [7:0] kin6,
  input  [7:0] kin14,
  input  [7:0] kin7,
  input  [7:0] kin15,
  input  clk,
  output [7:0] out0,
  output [7:0] out8,
  output [7:0] out1,
  output [7:0] out9,
  output [7:0] out2,
  output [7:0] out10,
  output [7:0] out3,
  output [7:0] out11,
  output [7:0] out4,
  output [7:0] out12,
  output [7:0] out5,
  output [7:0] out13,
  output [7:0] out6,
  output [7:0] out14,
  output [7:0] out7,
  output [7:0] out15,
  output [7:0] kout0,
  output [7:0] kout8,
  output [7:0] kout1,
  output [7:0] kout9,
  output [7:0] kout2,
  output [7:0] kout10,
  output [7:0] kout3,
  output [7:0] kout11,
  output [7:0] kout4,
  output [7:0] kout12,
  output [7:0] kout5,
  output [7:0] kout13,
  output [7:0] kout6,
  output [7:0] kout14,
  output [7:0] kout7,
  output [7:0] kout15
);

  Register register_1 (.D(in0), .Q(out0), .clk(clk));  // open: en, clr
  Register register_2 (.D(in1), .Q(out1), .clk(clk));  // open: en, clr
  Register register_3 (.D(in2), .Q(out2), .clk(clk));  // open: en, clr
  Register register_4 (.D(in3), .Q(out3), .clk(clk));  // open: en, clr
  Register register_5 (.D(in4), .Q(out4), .clk(clk));  // open: en, clr
  Register register_6 (.D(in5), .Q(out5), .clk(clk));  // open: en, clr
  Register register_7 (.D(in6), .Q(out6), .clk(clk));  // open: en, clr
  Register register_8 (.D(in7), .Q(out7), .clk(clk));  // open: en, clr
  Register register_9 (.D(kin0), .Q(kout0), .clk(clk));  // open: en, clr
  Register register_10 (.D(kin1), .Q(kout1), .clk(clk));  // open: en, clr
  Register register_11 (.D(kin2), .Q(kout2), .clk(clk));  // open: en, clr
  Register register_12 (.D(kin3), .Q(kout3), .clk(clk));  // open: en, clr
  Register register_13 (.D(kin4), .Q(kout4), .clk(clk));  // open: en, clr
  Register register_14 (.D(kin5), .Q(kout5), .clk(clk));  // open: en, clr
  Register register_15 (.D(kin6), .Q(kout6), .clk(clk));  // open: en, clr
  Register register_16 (.D(kin7), .Q(kout7), .clk(clk));  // open: en, clr
  Register register_17 (.D(in8), .Q(out8), .clk(clk));  // open: en, clr
  Register register_18 (.D(in9), .Q(out9), .clk(clk));  // open: en, clr
  Register register_19 (.D(in10), .Q(out10), .clk(clk));  // open: en, clr
  Register register_20 (.D(in11), .Q(out11), .clk(clk));  // open: en, clr
  Register register_21 (.D(in12), .Q(out12), .clk(clk));  // open: en, clr
  Register register_22 (.D(in13), .Q(out13), .clk(clk));  // open: en, clr
  Register register_23 (.D(in14), .Q(out14), .clk(clk));  // open: en, clr
  Register register_24 (.D(in15), .Q(out15), .clk(clk));  // open: en, clr
  Register register_25 (.D(kin8), .Q(kout8), .clk(clk));  // open: en, clr
  Register register_26 (.D(kin9), .Q(kout9), .clk(clk));  // open: en, clr
  Register register_27 (.D(kin10), .Q(kout10), .clk(clk));  // open: en, clr
  Register register_28 (.D(kin11), .Q(kout11), .clk(clk));  // open: en, clr
  Register register_29 (.D(kin12), .Q(kout12), .clk(clk));  // open: en, clr
  Register register_30 (.D(kin13), .Q(kout13), .clk(clk));  // open: en, clr
  Register register_31 (.D(kin14), .Q(kout14), .clk(clk));  // open: en, clr
  Register register_32 (.D(kin15), .Q(kout15), .clk(clk));  // open: en, clr
endmodule

// cm_col
module column_mix_col (
  input  [7:0] in0,
  input  [7:0] in1,
  input  [7:0] in2,
  input  [7:0] in3,
  output [7:0] out0,
  output [7:0] out1,
  output [7:0] out2,
  output [7:0] out3
);

  column_mix_elm column_mix_elm_1 (.in0(in0), .in1(in1), .in2(in2), .in3(in3), .out(out0));
  column_mix_elm column_mix_elm_2 (.in0(in1), .in1(in2), .in2(in3), .in3(in0), .out(out1));
  column_mix_elm column_mix_elm_3 (.in0(in2), .in1(in3), .in2(in0), .in3(in1), .out(out2));
  column_mix_elm column_mix_elm_4 (.in0(in3), .in1(in0), .in2(in1), .in3(in2), .out(out3));
endmodule

// cm_elm
module column_mix_elm (
  input  [7:0] in0,
  input  [7:0] in1,
  input  [7:0] in2,
  input  [7:0] in3,
  output [7:0] out
);

  wire [7:0] column_mix_mul0x2_1_out, column_mix_mul0x2_2_out, xor_1_out, xor_2_out, xor_3_out;

  column_mix_mul0x2 column_mix_mul0x2_1 (.in(in0), .out(column_mix_mul0x2_1_out));
  column_mix_mul0x2 column_mix_mul0x2_2 (.in(in1), .out(column_mix_mul0x2_2_out));
  assign xor_1_out = in1 ^ column_mix_mul0x2_2_out;  // XOR_Gate xor_1, 8 bits wide
  assign xor_2_out = column_mix_mul0x2_1_out ^ xor_1_out;  // XOR_Gate xor_2, 8 bits wide
  assign xor_3_out = in2 ^ in3;  // XOR_Gate xor_3, 8 bits wide
  assign out = xor_2_out ^ xor_3_out;  // XOR_Gate xor_4, 8 bits wide
endmodule

// cm_mul0x2
module column_mix_mul0x2 (
  input  [7:0] in,
  output [7:0] out
);

  wire [7:0] xor_1_out;

  assign xor_1_out = 8'h1b ^ {in[6:0], 1'b0};  // XOR_Gate xor_1, 8 bits wide
  Multiplexer #(.width(8)) multiplexer_1 (.in0({in[6:0], 1'b0}), .in1(xor_1_out), .out(out), .sel(in[7]));  // open: en
endmodule

// g
module key_gen_g (
  input  [31:0] in,
  input  [3:0] turn_number,
  output [31:0] out
);

  wire [7:0] rom_1_data, s_box_1_out;

  s_box s_box_1 (.in(in[23:16]), .out(s_box_1_out));
  s_box s_box_2 (.in(in[15:8]), .out(out[23:16]));
  s_box s_box_3 (.in(in[7:0]), .out(out[15:8]));
  s_box s_box_4 (.in(in[31:24]), .out(out[7:0]));
  ROM #(.addrWidth(4)) rom_1 (.addr(turn_number), .data(rom_1_data));  // open: sel
  assign out[31:24] = rom_1_data ^ s_box_1_out;  // XOR_Gate xor_1, 8 bits wide

  // Notes on the sheet:
  //   contents of rom_1 (hex, n*v repeats v):
  //   1 2 4 8 10 20 40 80 1b 36
endmodule

module s_box (
  input  [7:0] in,
  output [7:0] out
);

  ROM rom_1 (.addr(in), .data(out));  // open: sel

  // Notes on the sheet:
  //   contents of rom_1 (hex, n*v repeats v):
  //   63 7c 77 7b f2 6b 6f c5 30 1 67 2b fe d7 ab 76 ca 82 c9 7d fa 59 47 f0 ad d4 a2 af 9c a4 72 c0 b7 fd
  //   93 26 36 3f f7 cc 34 a5 e5 f1 71 d8 31 15 4 c7 23 c3 18 96 5 9a 7 12 80 e2 eb 27 b2 75 9 83 2c 1a 1b
  //   6e 5a a0 52 3b d6 b3 29 e3 2f 84 53 d1 0 ed 20 fc b1 5b 6a cb be 39 4a 4c 58 cf d0 ef aa fb 43 4d 33
  //   85 45 f9 2 7f 50 3c 9f a8 51 a3 40 8f 92 9d 38 f5 bc b6 da 21 10 ff f3 d2 cd c 13 ec 5f 97 44 17 c4
  //   a7 7e 3d 64 5d 19 73 60 81 4f dc 22 2a 90 88 46 ee b8 14 de 5e b db e0 32 3a a 49 6 24 5c c2 d3 ac
  //   62 91 95 e4 79 e7 c8 37 6d 8d d5 4e a9 6c 56 f4 ea 65 7a ae 8 ba 78 25 2e 1c a6 b4 c6 e8 dd 74 1f 4b
  //   bd 8b 8a 70 3e b5 66 48 3 f6 e 61 35 57 b9 86 c1 1d 9e e1 f8 98 11 69 d9 8e 94 9b 1e 87 e9 ce 55 28
  //   df 8c a1 89 d bf e6 42 68 41 99 2d f b0 54 bb 16
endmodule

module test_key_gen (
);

  wire key_gen_oneturn_1_p18, key_gen_oneturn_1_p19, key_gen_oneturn_1_p20, key_gen_oneturn_1_p21,
       key_gen_oneturn_1_p22, key_gen_oneturn_1_p23, key_gen_oneturn_1_p24, key_gen_oneturn_1_p25,
       key_gen_oneturn_1_p26, key_gen_oneturn_1_p27, key_gen_oneturn_1_p28, key_gen_oneturn_1_p29,
       key_gen_oneturn_1_p30, key_gen_oneturn_1_p31, key_gen_oneturn_1_p32, key_gen_oneturn_1_p33;

  // key_gen_oneturn key_gen_oneturn_1: pin names not known; wires that end beside it: 8'hf, 8'h15, 8'h71, 8'hc9, 8'h47, 8'hd9, 8'he8, 8'h59, 8'hc, 8'hb7, 8'had, 8'hd6, 8'haf, 8'h7f, 8'h67, 8'h98, 4'b0000, key_gen_oneturn_1_p18, key_gen_oneturn_1_p19, key_gen_oneturn_1_p20, key_gen_oneturn_1_p21, key_gen_oneturn_1_p22, key_gen_oneturn_1_p23, key_gen_oneturn_1_p24, key_gen_oneturn_1_p25, key_gen_oneturn_1_p26, key_gen_oneturn_1_p27, key_gen_oneturn_1_p28, key_gen_oneturn_1_p29, key_gen_oneturn_1_p30, key_gen_oneturn_1_p31, key_gen_oneturn_1_p32, key_gen_oneturn_1_p33
  // Probe on key_gen_oneturn_1_p18
  // Probe on key_gen_oneturn_1_p19
  // Probe on key_gen_oneturn_1_p20
  // Probe on key_gen_oneturn_1_p21
  // Probe on key_gen_oneturn_1_p22
  // Probe on key_gen_oneturn_1_p23
  // Probe on key_gen_oneturn_1_p24
  // Probe on key_gen_oneturn_1_p25
  // Probe on key_gen_oneturn_1_p26
  // Probe on key_gen_oneturn_1_p27
  // Probe on key_gen_oneturn_1_p28
  // Probe on key_gen_oneturn_1_p29
  // Probe on key_gen_oneturn_1_p30
  // Probe on key_gen_oneturn_1_p31
  // Probe on key_gen_oneturn_1_p32
  // Probe on key_gen_oneturn_1_p33
endmodule
